# Fritzing sketch tape_following_circuitry (saved by Fritzing 0.9.2b)
breadboards: 3

parts:
  Part1 = Arduino Motor Shield (Rev3)
  Q3 = PHOTOTRANSISTOR REFLECTIVE OBJECT SENSOR [package=qrb1114-side]
  Q4 = PHOTOTRANSISTOR REFLECTIVE OBJECT SENSOR [package=qrb1114-side]
  R5 = Resistor [tolerance=±5% resistance=220 package="2010 [SMD]"]
  R6 = Resistor [tolerance=±5% resistance=220 package="2010 [SMD]"]
  R7 = Resistor [tolerance=±5% resistance=10k package="2010 [SMD]"]
  R8 = Resistor [tolerance=±5% resistance=10k package="2010 [SMD]"]
  Composant4 = SRF05 Ultrasonic Rangefinder  # not connected
  M1 = DC Motor
  M2 = DC Motor

nets:
  N1: Part1.A1, Part1.5V
  N2: Part1.B-, M1.pin_2
  N3: Part1.B+, M1.pin_1
  N4: Part1.A-, M2.pin_2
  N5: Part1.A+, M2.pin_1
  N6: Q3.A, R8.Pin_0
  N7: Q3.C, R5.Pin_0
  N8: Q3.E, Q3.K
  N9: Q4.A, R7.Pin_0
  N10: Q4.C, R6.Pin_0
  N11: Q4.E, Q4.K, R5.Pin_1, R6.Pin_1, R7.Pin_1, R8.Pin_1

notes:
  to tape
  TO HUB
  HUB
  TAPE
  Range
  to range
  Braid wires to motors to reduce intereference
